# Fritzing sketch SmartShunt (saved by Fritzing 0.9.10b)
breadboards: 1

parts:
  WeMos_D1_Mini1 = WeMos D1 Mini
  INR226 = INA226 Module
  Bauteil3 = FTDI Basic Programmer

nets:
  3V3: WeMos_D1_Mini1.3V3, INR226.VCC, Bauteil3.POWER
  N1: WeMos_D1_Mini1.D1, INR226.SCL
  N2: WeMos_D1_Mini1.D2, INR226.SDA
  N3: WeMos_D1_Mini1.D5, INR226.ALE
  GND: WeMos_D1_Mini1.G, INR226.GND, Bauteil3.GND
  N4: WeMos_D1_Mini1.RX, Bauteil3.TXO
  N5: WeMos_D1_Mini1.TX, Bauteil3.RXI
